# Fritzing sketch Sensor de golpe (saved by Fritzing 0.9.3b)

parts:
  U1 = ESP32-38PinWide [part_number=ESP32-38PinWide]
  Mod1 = KY-031 Knock Sensor Module [package="Breakout board"]

nets:
  VIN: U1.VIN, Mod1.Vin
  N1: U1.GPIO16, Mod1.S
  N2: U1.GND, Mod1.-

custom parts:
  ESP32-38PinWide: Generic 38-Pin ESP32 with wide format (only access to one side of pins on a breadboard) based on Stephen Lilley's HiLetgo ESP-WROOM-32 ESP32 ESP-32S Development Board.
  KY-031 Knock Sensor Module: KY-031 Knock Sensor module. A vibration sensor that sends a signal when a knock/tap is detected.
